# Fritzing sketch Kuldvillaku skeem (saved by Fritzing 0.9.3b)
breadboards: 1

parts:
  R1 = Resistor [tolerance=±5% resistance=220 package=THT]
  R2 = Resistor [tolerance=±5% resistance=220 package=THT]
  R3 = Resistor [tolerance=±5% resistance=220 package=THT]
  R4 = Resistor [tolerance=±5% resistance=220 package=THT]
  S1 = SWITCH-MOMENTARY-2 [package=tactile_switch_smd-2]
  S2 = SWITCH-MOMENTARY-2 [package=tactile_switch_smd-2]
  S3 = SWITCH-MOMENTARY-2 [package=tactile_switch_smd-2]
  S4 = SWITCH-MOMENTARY-2 [package=tactile_switch_smd-2]
  Arduino_Nano = Arduino Nano (Rev3.0)
  RGB_LED = RGB LED (com. anode, rbg) [package="5 mm [THT]"]
  R5 = Resistor [tolerance=±5% resistance=220 package="2512 [SMD]"]
  R6 = Resistor [tolerance=±5% resistance=220 package="2512 [SMD]"]
  R7 = Resistor [tolerance=±5% resistance=220 package="2512 [SMD]"]
  Power_Switch = Toggle Switch [package=THT]
  BAT1 = BC9VPC [package=bc9vpc]

nets:
  N1: R1.Pin_0, R2.Pin_0, R3.Pin_0, R4.Pin_0, Arduino_Nano.GND, BAT1.V-
  N2: R1.Pin_1, S1.2, Arduino_Nano.D12/MISO
  N3: R2.Pin_1, S2.2, Arduino_Nano.D10
  N4: R3.Pin_1, S3.2, Arduino_Nano.D8
  N5: R4.Pin_1, S4.2, Arduino_Nano.D6
  N6: S1.1, S2.1, S3.1, S4.1, Arduino_Nano.5V, RGB_LED.common_anode
  N7: Arduino_Nano.D5, R6.Pin_1
  N8: Arduino_Nano.D9, R5.Pin_1
  N9: Arduino_Nano.D11/MOSI, R7.Pin_1
  N10: Arduino_Nano.VIN, Power_Switch.L2
  N11: RGB_LED.red_cathode, R5.Pin_0
  N12: RGB_LED.blue_cathode, R6.Pin_0
  N13: RGB_LED.green_cathode, R7.Pin_0
  N14: Power_Switch.COM, BAT1.V+
